# Fritzing sketch raspi-emic (saved by Fritzing 0.9.0b)

parts:
  Part1 = EMIC2
  Part2 = Logic Level Converter
  Raspberry_Pi_B_rev1 = Raspberry Pi B rev2

nets:
  GND: Part1.GND, Part2.GND, Part2.RX_LV, Raspberry_Pi_B_rev1.GND
  5V: Part1.5V, Part2.HV, Raspberry_Pi_B_rev1.5V
  N1: Part1.SOUT, Part2.RX_HV
  N2: Part1.SIN, Part1.SP-, Part2.TX_HV
  N3: Part2.LV, Raspberry_Pi_B_rev1.3V3
  N4: Part2.TX_LV, Raspberry_Pi_B_rev1.GPIO_14
